// Logisim project Logisim.circ as structural Verilog: 14 circuits, main circuit main
module main (
  input  A,
  input  B,
  input  C,
  input  D,
  input  S,
  output A_prime,
  output A_prime_2,
  output A_B__prime,
  output A_B__prime_2,
  output A_B_C__prime,
  output A_B_C__prime_2,
  output A_B__prime_3,
  output A_B__prime_4,
  output A_B_C__prime_3,
  output A_B_C__prime_4,
  output A_B_prime___A_prime_B,
  output A_B_prime___A_prime_B_2,
  output A_B___A_prime_B_prime,
  output A_B___A_prime_B_prime_2,
  output A_B___C_D___prime,
  output A_B___C_D___prime_2,
  output A_B___C_D___prime_3,
  output A_B___C_D___prime_4,
  output A_S_prime___B_S,
  output A_S_prime___B_S_2
);

  INV inv_1 (.A(A), .Z(A_prime));
  NAND2 nand2_1 (.A(A), .B(B), .Z(A_B__prime));
  NAND3 nand3_1 (.A(A), .B(B), .C(C), .Z(A_B_C__prime));
  NOR2 nor2_1 (.A(A), .B(B), .Z(A_B__prime_3));
  NOR3 nor3_1 (.A(A), .B(B), .C(C), .Z(A_B_C__prime_3));
  XOR2 xor2_1 (.A(A), .B(B), .Z(A_B_prime___A_prime_B));
  XNOR2 xnor2_1 (.A(A), .B(B), .Z(A_B___A_prime_B_prime));
  AOI22 aoi22_1 (.A(A), .B(B), .C(C), .D(D), .Z(A_B___C_D___prime));
  OAI22 oai22_1 (.A(A), .B(B), .C(C), .D(D), .Z(A_B___C_D___prime_3));
  MUX2x1 mux2x1_1 (.A(A), .S(S), .B(B), .Z(A_S_prime___B_S));
  not not_1 (A_prime_2, A);
  nand nand_1 (A_B__prime_2, A, B);
  nand nand_2 (A_B_C__prime_2, A, B, C);
  nor nor_1 (A_B__prime_4, A, B);
  nor nor_2 (A_B_C__prime_4, A, B, C);
  xor xor_1 (A_B_prime___A_prime_B_2, A, B);
  xnor xnor_1 (A_B___A_prime_B_prime_2, A, B);
  AOI22_Cir aoi22_cir_1 (.Input_0(A), .Input_1(B), .Input_2(C), .Input_3(D), .Output_0(A_B___C_D___prime_2));
  OAI22_Cir oai22_cir_1 (.Input_0(A), .Input_1(B), .Input_2(C), .Input_3(D), .Output_0(A_B___C_D___prime_4));
  Multiplexer #(.enable("false")) multiplexer_1 (.in0(A), .in1(B), .out(A_S_prime___B_S_2), .sel(S));
endmodule

module INV (
  input  A,
  output Z
);

  Transistor transistor_1 (.in(1'b1), .out(Z), .gate(A));
  Transistor #(.\type ("n")) transistor_2 (.in(1'b0), .out(Z), .gate(A));

  // Notes on the sheet:
  //   CMOS INVERTER GATE TRANSISTOR LEVEL DESIGN
  //   VDD
  //   GND
endmodule

module NAND2 (
  input  A,
  input  B,
  output Z
);

  wire transistor_4_out;

  Transistor transistor_1 (.in(1'b1), .out(Z), .gate(A));
  Transistor transistor_2 (.in(1'b1), .out(Z), .gate(B));
  Transistor #(.\type ("n")) transistor_3 (.in(transistor_4_out), .out(Z), .gate(A));
  Transistor #(.\type ("n")) transistor_4 (.in(1'b0), .out(transistor_4_out), .gate(B));

  // Notes on the sheet:
  //   CMOS 2-INPUT NAND GATE TRANSISTOR LEVEL DESIGN
  //   VDD
  //   GND
endmodule

module NAND3 (
  input  A,
  input  B,
  input  C,
  output Z
);

  wire transistor_5_out, transistor_6_out;

  Transistor transistor_1 (.in(1'b1), .out(Z), .gate(B));
  Transistor transistor_2 (.in(1'b1), .out(Z), .gate(A));
  Transistor transistor_3 (.in(1'b1), .out(Z), .gate(C));
  Transistor #(.\type ("n")) transistor_4 (.in(transistor_5_out), .out(Z), .gate(A));
  Transistor #(.\type ("n")) transistor_5 (.in(transistor_6_out), .out(transistor_5_out), .gate(B));
  Transistor #(.\type ("n")) transistor_6 (.in(1'b0), .out(transistor_6_out), .gate(C));

  // Notes on the sheet:
  //   CMOS 3-INPUT NAND GATE TRANSISTOR LEVEL DESIGN
  //   VDD
  //   GND
endmodule

module NOR2 (
  input  A,
  input  B,
  output Z
);

  wire transistor_2_out;

  Transistor #(.\type ("n")) transistor_1 (.in(1'b0), .out(Z), .gate(A));
  Transistor transistor_2 (.in(1'b1), .out(transistor_2_out), .gate(A));
  Transistor transistor_3 (.in(transistor_2_out), .out(Z), .gate(B));
  Transistor #(.\type ("n")) transistor_4 (.in(1'b0), .out(Z), .gate(B));

  // Notes on the sheet:
  //   CMOS 2-INPUT NOR GATE TRANSISTOR LEVEL DESIGN
  //   VDD
  //   GND
endmodule

module NOR3 (
  input  A,
  input  B,
  input  C,
  output Z
);

  wire transistor_3_out, transistor_4_out;

  Transistor #(.\type ("n")) transistor_1 (.in(1'b0), .out(Z), .gate(A));
  Transistor #(.\type ("n")) transistor_2 (.in(1'b0), .out(Z), .gate(B));
  Transistor transistor_3 (.in(1'b1), .out(transistor_3_out), .gate(A));
  Transistor transistor_4 (.in(transistor_3_out), .out(transistor_4_out), .gate(B));
  Transistor transistor_5 (.in(transistor_4_out), .out(Z), .gate(C));
  Transistor #(.\type ("n")) transistor_6 (.in(1'b0), .out(Z), .gate(C));

  // Notes on the sheet:
  //   CMOS 3-INPUT NOR GATE TRANSISTOR LEVEL DESIGN
  //   VDD
  //   GND
endmodule

module XOR2 (
  input  A,
  input  B,
  output Z
);

  wire not_1_out, not_2_out, transistor_1_out, transistor_4_out, transistor_5_out, transistor_8_out;

  not not_1 (not_1_out, A);
  not not_2 (not_2_out, B);
  Transistor transistor_1 (.in(1'b1), .out(transistor_1_out), .gate(A));
  Transistor transistor_2 (.in(transistor_1_out), .out(Z), .gate(not_2_out));
  Transistor #(.\type ("n")) transistor_3 (.in(transistor_4_out), .out(Z), .gate(A));
  Transistor #(.\type ("n")) transistor_4 (.in(1'b0), .out(transistor_4_out), .gate(B));
  Transistor transistor_5 (.in(1'b1), .out(transistor_5_out), .gate(not_1_out));
  Transistor transistor_6 (.in(transistor_5_out), .out(Z), .gate(B));
  Transistor #(.\type ("n")) transistor_7 (.in(transistor_8_out), .out(Z), .gate(not_1_out));
  Transistor #(.\type ("n")) transistor_8 (.in(1'b0), .out(transistor_8_out), .gate(not_2_out));

  // Notes on the sheet:
  //   A'
  //   B'
  //   CMOS 2-INPUT XOR GATE TRANSISTOR LEVEL DESIGN
  //   VDD
  //   GND
endmodule

module XNOR2 (
  input  A,
  input  B,
  output Z
);

  wire not_1_out, not_2_out, transistor_1_out, transistor_4_out, transistor_5_out, transistor_8_out;

  not not_1 (not_1_out, A);
  not not_2 (not_2_out, B);
  Transistor transistor_1 (.in(1'b1), .out(transistor_1_out), .gate(A));
  Transistor transistor_2 (.in(transistor_1_out), .out(Z), .gate(B));
  Transistor #(.\type ("n")) transistor_3 (.in(transistor_4_out), .out(Z), .gate(A));
  Transistor #(.\type ("n")) transistor_4 (.in(1'b0), .out(transistor_4_out), .gate(not_2_out));
  Transistor transistor_5 (.in(1'b1), .out(transistor_5_out), .gate(not_1_out));
  Transistor transistor_6 (.in(transistor_5_out), .out(Z), .gate(not_2_out));
  Transistor #(.\type ("n")) transistor_7 (.in(transistor_8_out), .out(Z), .gate(not_1_out));
  Transistor #(.\type ("n")) transistor_8 (.in(1'b0), .out(transistor_8_out), .gate(B));

  // Notes on the sheet:
  //   A'
  //   B'
  //   CMOS 2-INPUT XNOR GATE TRANSISTOR LEVEL DESIGN
  //   VDD
  //   GND
endmodule

module AOI22 (
  input  A,
  input  B,
  input  C,
  input  D,
  output Z
);

  wire transistor_1_out, transistor_7_out, transistor_8_out;

  Transistor transistor_1 (.in(1'b1), .out(transistor_1_out), .gate(B));
  Transistor transistor_2 (.in(1'b1), .out(transistor_1_out), .gate(A));
  Transistor transistor_3 (.in(transistor_1_out), .out(Z), .gate(C));
  Transistor transistor_4 (.in(transistor_1_out), .out(Z), .gate(D));
  Transistor #(.\type ("n")) transistor_5 (.in(transistor_8_out), .out(Z), .gate(C));
  Transistor #(.\type ("n")) transistor_6 (.in(transistor_7_out), .out(Z), .gate(A));
  Transistor #(.\type ("n")) transistor_7 (.in(1'b0), .out(transistor_7_out), .gate(B));
  Transistor #(.\type ("n")) transistor_8 (.in(1'b0), .out(transistor_8_out), .gate(D));

  // Notes on the sheet:
  //   CMOS 4-INPUT AOI22 CELL TRANSISTOR LEVEL DESIGN
  //   VDD
  //   GND
endmodule

module OAI22 (
  input  A,
  input  B,
  input  C,
  input  D,
  output Z
);

  wire transistor_1_out, transistor_2_out, transistor_7_out;

  Transistor transistor_1 (.in(1'b1), .out(transistor_1_out), .gate(A));
  Transistor transistor_2 (.in(1'b1), .out(transistor_2_out), .gate(C));
  Transistor transistor_3 (.in(transistor_1_out), .out(Z), .gate(B));
  Transistor transistor_4 (.in(transistor_2_out), .out(Z), .gate(D));
  Transistor #(.\type ("n")) transistor_5 (.in(transistor_7_out), .out(Z), .gate(B));
  Transistor #(.\type ("n")) transistor_6 (.in(transistor_7_out), .out(Z), .gate(A));
  Transistor #(.\type ("n")) transistor_7 (.in(1'b0), .out(transistor_7_out), .gate(C));
  Transistor #(.\type ("n")) transistor_8 (.in(1'b0), .out(transistor_7_out), .gate(D));

  // Notes on the sheet:
  //   CMOS 4-INPUT OAI22 CELL TRANSISTOR LEVEL DESIGN
  //   VDD
  //   GND
endmodule

module MUX2x1 (
  input  A,
  input  S,
  input  B,
  output Z
);

  wire transistor_1_out;

  Transistor transistor_1 (.in(1'b1), .out(transistor_1_out), .gate(S));
  Transistor #(.\type ("n")) transistor_2 (.in(1'b0), .out(transistor_1_out), .gate(S));
  Transistor transistor_3 (.in(A), .out(Z), .gate(S));
  Transistor #(.\type ("n"), .gate("br")) transistor_4 (.in(A), .out(Z), .gate(transistor_1_out));
  Transistor transistor_5 (.in(B), .out(Z), .gate(transistor_1_out));
  Transistor #(.\type ("n"), .gate("br")) transistor_6 (.in(B), .out(Z), .gate(S));

  // Notes on the sheet:
  //   VDD
  //   CMOS 2:1 MUX TRANSISTOR LEVEL DESIGN
  //   (with transmission gates)
  //   GND
endmodule

module MUX2x1_2 (
  input  S,
  input  A,
  input  B,
  output Z
);

  wire not_1_out, transistor_1_out, transistor_4_out, transistor_5_out, transistor_8_out;

  not not_1 (not_1_out, S);
  Transistor transistor_1 (.in(1'b1), .out(transistor_1_out), .gate(A));
  Transistor transistor_2 (.in(transistor_1_out), .out(Z), .gate(not_1_out));
  Transistor #(.\type ("n")) transistor_3 (.in(transistor_4_out), .out(Z), .gate(A));
  Transistor #(.\type ("n")) transistor_4 (.in(1'b0), .out(transistor_4_out), .gate(S));
  Transistor transistor_5 (.in(1'b1), .out(transistor_5_out), .gate(B));
  Transistor transistor_6 (.in(transistor_5_out), .out(Z), .gate(S));
  Transistor #(.\type ("n")) transistor_7 (.in(transistor_8_out), .out(Z), .gate(B));
  Transistor #(.\type ("n")) transistor_8 (.in(1'b0), .out(transistor_8_out), .gate(not_1_out));

  // Notes on the sheet:
  //   CMOS 2:1 MUX TRANSISTOR LEVEL DESIGN
  //   VDD
  //   GND
endmodule

module AOI22_Cir (
  input  Input_0,
  input  Input_1,
  input  Input_2,
  input  Input_3,
  output Output_0
);

  wire and_1_out, and_2_out, or_1_out;

  and and_1 (and_1_out, Input_0, Input_1);
  and and_2 (and_2_out, Input_2, Input_3);
  or or_1 (or_1_out, and_1_out, and_2_out);
  not not_1 (Output_0, or_1_out);
endmodule

module OAI22_Cir (
  input  Input_0,
  input  Input_1,
  input  Input_2,
  input  Input_3,
  output Output_0
);

  wire and_1_out, or_1_out, or_2_out;

  or or_1 (or_1_out, Input_0, Input_1);
  or or_2 (or_2_out, Input_2, Input_3);
  not not_1 (Output_0, and_1_out);
  and and_1 (and_1_out, or_1_out, or_2_out);
endmodule
